# Fritzing sketch receptor y foco (saved by Fritzing 0.8.7b)
breadboards: 1

parts:
  Parte1 = Arduino Uno (Rev3)
  U2 = XD-RF-5V [package=THT]
  U3 = 2-Channel 5v Relay Shield [package=relay-2ch5v10a]
  LED1 = LEDs [package=led10mm]
  Power_plug1 = Power plug

nets:
  N1: Parte1.D2, U3.IN1
  N2: Parte1.D3_PWM, U2.DATA#2
  VCC: Parte1.5V, U2.VCC, U3.VCC
  GND: Parte1.GND, U2.GND, U3.GND
  N3: U3.K1-In, Power_plug1.GND
  N4: U3.K1-On, LED1.C
  N5: LED1.A, Power_plug1.VCC

notes:
  CORRIENTE ALTERNA
  220V
  Rojo = Fase
  Negro = Neutro
  Compra estos materiales en www.nova.com.bo
  conectar cualquiera de los 2 pines del medio al pin 3 del arduino

custom parts:
  XD-RF-5V: This is 433Mhz RF transmitter with receiver kit for Arduino ARM MCU wireless Application environment: Remote control switch, receiver module, motorcycles, automobile anti-theft products, home security products, electric doors, shutter doors, windows, remote control socket, remote control LED, remote audio remote control electric doors, garage door remote control, remote control retractable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
  2-Channel 5v Relay Shield: 2 Channel 5v Relay Shield w. 2x SPD-06VDC-SD-C
  LEDs: LEDs Standard schematic elements and footprints for 5mm, 3mm, 1206, and 0603 sized LEDs. 5mm - Spark Fun Electronics SKU : COM-00529 (and others)
