# Fritzing sketch esquema transmisor con pulsador (saved by Fritzing 0.8.7b)
breadboards: 1

parts:
  Parte1 = Arduino Uno (Rev3)
  U1 = FS1000A - 433Mhz RF Transmitter [package=THT]
  S1 = Pushbutton [package="[THT]"]
  R1 = Resistor [tolerance=±5% resistance=220 package=THT]

nets:
  N1: Parte1.D12/MISO, U1.DATA
  N2: Parte1.D2, S1.Pin_3, S1.Pin_4, R1.Pin_0
  5V: Parte1.5V, U1.VCC, S1.Pin_1, S1.Pin_2
  GND: Parte1.GND, U1.GND, R1.Pin_1

notes:
  Compra estos materiales en www.nova.com.bo
  Conectar ATAD al pin 12 del arduino

custom parts:
  FS1000A - 433Mhz RF Transmitter: This is 433Mhz RF transmitter with receiver kit for Arduino ARM MCU wireless Application environment: Remote control switch, receiver module, motorcycles, automobile anti-theft products, home security products, electric doors, shutter doors, windows, remote control socket, remote control LED, remote audio remote control electric doors, garage door remote control, remote control retractable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
